// Logisim project Parity_Error_Detection (1).circ as structural Verilog: 1 circuit, main circuit main
module main (
  input  D1,
  input  D2,
  input  D3,
  input  D4,
  input  P,
  output LED
);

  wire XOR_2_out, XOR_3_out, XOR_out;

  xor XOR (XOR_out, D1, D2);
  xor XOR_2 (XOR_2_out, XOR_out, D3);
  xor XOR_3 (XOR_3_out, XOR_2_out, D4);
  xor XOR_4 (LED, XOR_3_out, P);
endmodule
