// Logisim project PARITY_CHECKER (2).circ as structural Verilog: 1 circuit, main circuit main
module main (
  input  D0,
  input  D1,
  input  D2,
  input  D3,
  input  P,
  output out_6
);

  wire XOR_A_out, XOR_B_out, XOR_C_out;

  xor XOR_A (XOR_A_out, D0, D1);
  xor XOR_B (XOR_B_out, D2, D3);
  xor XOR_D (out_6, XOR_C_out, P);
  xor XOR_C (XOR_C_out, XOR_A_out, XOR_B_out);
endmodule
