// Logisim project PARITY_GENRATOR (2).circ as structural Verilog: 1 circuit, main circuit main
module main (
  input  D0,
  input  D1,
  input  D2,
  input  D3,
  output P__PARITY
);

  wire XOR_1_out, XOR_2_out;

  xor XOR_1 (XOR_1_out, D0, D1);
  xor XOR_2 (XOR_2_out, D2, D3);
  xor XOR_3 (P__PARITY, XOR_1_out, XOR_2_out);
endmodule
